# Fritzing sketch robot-motor (saved by Fritzing 0.9.2b)
breadboards: 1

parts:
  Part1 = Arduino Uno (Rev3)
  M1 = DC Motor  # not connected
  M2 = DC Motor  # not connected
  IC1 = IC, DIP package, 16 pins [chip_label=IC]  # not connected
  VCC1 = Battery block 9V
  Arduino_5V_power_Source = 4 x AAA Battery Mount  # not connected

nets:
  N1: Part1.GND, VCC1.-
