# Fritzing sketch robot (saved by Fritzing 0.9.2b)
breadboards: 1

parts:
  Part1 = Arduino Uno (Rev3)
  M1 = DC Motor  # not connected
  M2 = DC Motor  # not connected
  IC1 = IC, DIP package, 16 pins [chip_label=IC]  # not connected
  VCC1 = Battery block 9V
  Part2 = SRF05 Ultrasonic Rangefinder
  J1 = Piezo Speaker
  Motion_Sensor = mystery part, 3 pins [chip_label="Motion Sensor" part_number="Pin Order(5v,Out,Ground)"]
  LDR = mystery part, 3 pins [chip_label="LDR " part_number="Pin Order (VCC,Ground, DO)"]
  Temperature = mystery part, 3 pins [chip_label=? part_number="Pin Order (+, out , -)"]
  Bluetooth = mystery part, 4 pins [chip_label=Bluetooth part_number="Pin Order(RX,TX,GND,VCC)"]
  Arduino_5V_power_Source = 4 x AAA Battery Mount  # not connected

nets:
  N1: Part1.D11_PWM/MOSI, Motion_Sensor.pin2
  N2: Part1.D12/MISO, Part2.connector10
  N3: Part1.D13/SCK, Part2.connector9
  N4: Part1.D0/RX, Bluetooth.pin2
  N5: Part1.D1/TX, Bluetooth.pin1
  N6: Part1.D4, LDR.pin3
  N7: Part1.D5_PWM, Temperature.pin2
  N8: Part1.D6_PWM, J1.pin2
  N9: Part1.5V, Part2.connector8, Motion_Sensor.pin1, LDR.pin1, Temperature.pin1, Bluetooth.pin4
  N10: Part1.GND, VCC1.-, Part2.connector11, J1.pin1, Motion_Sensor.pin3, LDR.pin2, Temperature.pin3, Bluetooth.pin3
