# Fritzing sketch Diagram (saved by Fritzing 0.9.2b)

parts:
  S1 = H-Bridge with L298N
  Part1 = Arduino Uno (Rev3) - ICSP
  BAT1 = BC9VPC [package=bc9vpc]
  M1 = DC Motor  # not connected
  M2 = DC Motor

nets:
  N1: S1.12V, BAT1.V+
  N2: S1.GND, BAT1.V-
  N3: S1.IN1, Part1.D7
  N4: S1.IN2, Part1.D8
  N5: S1.IN3, Part1.D9_PWM
  N6: S1.IN4, Part1.D11_PWM/MOSI
  N7: S1.OUT4-Motor2, M2.pin_2

notes:
  ENA, ENB , Connect to the motor - order doesnt matter

custom parts:
  H-Bridge with L298N: h-bridge
