# Fritzing sketch onlyController (saved by Fritzing 0.9.2b)

parts:
  Part1 = Arduino Uno (Rev3)
  S1 = H-Bridge with L298N
  M1 = DC Motor
  M2 = DC Motor
  BAT1 = BC9VPC [package=bc9vpc]

nets:
  N1: Part1.D8, S1.IN2
  N2: Part1.D4, S1.IN3
  N3: Part1.D6_PWM, S1.IN4
  N4: Part1.D7, S1.IN1
  N5: S1.12V, BAT1.V+
  N6: S1.GND, BAT1.V-
  N7: S1.OUT4-Motor2, M2.pin_1
  N8: S1.OUT2-Motor1, M1.pin_2

notes:
  ENA
  ENB
  These are the two pins on either sides of the 'IN#' pins on the motor controller board

custom parts:
  H-Bridge with L298N: h-bridge
