# Fritzing sketch lightSensor (saved by Fritzing 0.9.2b)
breadboards: 1

parts:
  Part1 = Arduino Uno (Rev3)
  LightSensor = mystery part, 3 pins [chip_label=LDR]

nets:
  N1: Part1.A1, LightSensor.pin1
  N2: Part1.5V, LightSensor.pin3
  N3: Part1.GND, LightSensor.pin2

notes:
  Vcc
  Grnd
  DO
