# Fritzing sketch motionSensor (saved by Fritzing 0.9.2b)
breadboards: 1

parts:
  Part1 = Arduino Uno (Rev3)
  MotionSensor = mystery part, 3 pins [chip_label=PIR]

nets:
  N1: Part1.A3, MotionSensor.pin2
  N2: Part1.5V, MotionSensor.pin3
  N3: Part1.GND, MotionSensor.pin1

notes:
  Vcc
  Out
  Grnd
