# Fritzing sketch sonarSensor (saved by Fritzing 0.9.2b)
breadboards: 1

parts:
  Part1 = Arduino Uno (Rev3)
  Part3 = SRF05 Ultrasonic Rangefinder

nets:
  N1: Part1.A4/SDA, Part3.Trig
  N2: Part1.A5/SCL, Part3.Echo
  5V: Part1.5V, Part3.VCC
  GND: Part1.GND, Part3.GND
