# Fritzing sketch sonarWithBuzzer (saved by Fritzing 0.9.2b)
breadboards: 1

parts:
  Part1 = Arduino Uno (Rev3)
  J1 = Piezo Speaker
  Part3 = SRF05 Ultrasonic Rangefinder

nets:
  N1: Part1.A0, J1.pin2
  N2: Part1.A4/SDA, Part3.Trig
  N3: Part1.A5/SCL, Part3.Echo
  5V: Part1.5V, Part3.VCC
  GND: Part1.GND, J1.pin1, Part3.GND
