# Fritzing sketch temperatureSensor (saved by Fritzing 0.9.2b)
breadboards: 1

parts:
  Part1 = Arduino Uno (Rev3)
  TemperatureSensor = mystery part, 3 pins [chip_label=DHT]

nets:
  N1: Part1.A2, TemperatureSensor.pin2
  N2: Part1.5V, TemperatureSensor.pin3
  N3: Part1.GND, TemperatureSensor.pin1

notes:
  +
  out
  -
