# Fritzing sketch pushAllSensorData (saved by Fritzing 0.9.2b)
breadboards: 1

parts:
  Part1 = Arduino Uno (Rev3)
  J1 = Piezo Speaker
  TemperatureSensor = mystery part, 3 pins [chip_label=DHT]
  LightSensor = mystery part, 3 pins [chip_label=LDR]
  MotionSensor = mystery part, 3 pins [chip_label=PIR]
  Part3 = SRF05 Ultrasonic Rangefinder

nets:
  N1: Part1.A0, J1.pin2
  N2: Part1.A1, LightSensor.pin1
  N3: Part1.A2, TemperatureSensor.pin2
  N4: Part1.A3, MotionSensor.pin2
  N5: Part1.A4/SDA, Part3.Trig
  N6: Part1.A5/SCL, Part3.Echo
  5V: Part1.5V, TemperatureSensor.pin3, LightSensor.pin3, MotionSensor.pin3, Part3.VCC
  GND: Part1.GND, J1.pin1, TemperatureSensor.pin1, LightSensor.pin2, MotionSensor.pin1, Part3.GND

notes:
  +
  out
  -
  Vcc
  Grnd
  DO
  Vcc
  Out
  Grnd
