# Fritzing sketch Diagram (saved by Fritzing 0.9.2b)
breadboards: 1

parts:
  S1 = H-Bridge with L298N
  Part1 = Arduino Uno (Rev3) - ICSP
  BAT1 = BC9VPC [package=bc9vpc]
  M1 = DC Motor  # not connected
  M2 = DC Motor
  Part2 = SRF05 Ultrasonic Rangefinder
  LDR1 = mystery part, 3 pins [chip_label="LDR " part_number="Pin Order (VCC,Ground, DO)"]
  Temperature1 = mystery part, 3 pins [chip_label=? part_number="Pin Order (+, out , -)"]
  Motion_Sensor1 = mystery part, 3 pins [chip_label="Motion Sensor" part_number="Pin Order(5v,Out,Ground)"]
  J2 = Piezo Speaker

nets:
  N1: S1.12V, BAT1.V+
  N2: S1.GND, BAT1.V-
  N3: S1.IN1, Part1.D7
  N4: S1.IN2, Part1.D8
  N5: S1.IN3, Part1.D9_PWM
  N6: S1.IN4, Part1.D11_PWM/MOSI
  N7: S1.OUT4-Motor2, M2.pin_2
  N8: Part1.A1, LDR1.pin3
  N9: Part1.D12/MISO, Temperature1.pin2
  N10: Part1.D13/SCK, Motion_Sensor1.pin2
  GND: Part1.GND, Part2.GND, LDR1.pin2, Temperature1.pin3, Motion_Sensor1.pin3, J2.pin1
  N11: Part1.D2, Part2.Trig
  N12: Part1.D4, Part2.Echo
  N13: Part1.D6_PWM, J2.pin2
  5V: Part1.5V, Part2.VCC, LDR1.pin1, Temperature1.pin1, Motion_Sensor1.pin1

notes:
  ENA, ENB connect to 5v

custom parts:
  H-Bridge with L298N: h-bridge
