# Fritzing sketch schematicsGuide (saved by Fritzing 0.9.2b)
breadboards: 1

parts:
  Part1 = Arduino Uno (Rev3)
  S1 = H-Bridge with L298N
  M1 = DC Motor
  M2 = DC Motor
  BAT1 = BC9VPC [package=bc9vpc]
  J1 = Piezo Speaker
  TemperatureSensor = mystery part, 3 pins [chip_label=DHT]
  LightSensor = mystery part, 3 pins [chip_label=LDR]
  MotionSensor = mystery part, 3 pins [chip_label=PIR]
  Part3 = SRF05 Ultrasonic Rangefinder

nets:
  N1: Part1.A0, J1.pin2
  N2: Part1.A1, LightSensor.pin1
  N3: Part1.A2, TemperatureSensor.pin2
  N4: Part1.A3, MotionSensor.pin2
  N5: Part1.A4/SDA, Part3.Trig
  N6: Part1.A5/SCL, Part3.Echo
  N7: Part1.D8, S1.IN2
  N8: Part1.D4, S1.IN3
  N9: Part1.D6_PWM, S1.IN4
  N10: Part1.D7, S1.IN1
  5V: Part1.5V, TemperatureSensor.pin3, LightSensor.pin3, MotionSensor.pin3, Part3.VCC
  GND: Part1.GND, J1.pin1, TemperatureSensor.pin1, LightSensor.pin2, MotionSensor.pin1, Part3.GND
  N11: S1.12V, BAT1.V+
  N12: S1.GND, BAT1.V-
  N13: S1.OUT4-Motor2, M2.pin_1
  N14: S1.OUT2-Motor1, M1.pin_2

notes:
  ENA
  ENB
  These are the two pins on either sides of the 'IN#' pins on the motor controller board
  +
  out
  -
  Vcc
  Grnd
  DO
  Vcc
  Out
  Grnd

custom parts:
  H-Bridge with L298N: h-bridge
